# Fritzing sketch circuit_diagram (saved by Fritzing 0.9.3b)

parts:
  Part1 = Arduino Mega ADK (Rev3)
  S1 = H-Bridge with L298N
  S2 = H-Bridge with L298N
  Raspberry_Pi_1 = Raspberry Pi 3 [part_number=RPI-3-V1.2]  # not connected
  BATT1 = LiPoly Battery (1300mAh)
  U1 = 2-Channel 5v Relay Shield [package=relay-2ch5v10a]
  DC_Mot_Enc1 = DC Motor with two-phase hall-encoder [part_number=VT-E-G25A-06-177E]
  X1 = USB Connectors [package=usb-a-s-nosilk]
  X2 = USB Connectors [package=usb-b-pth]
  X3 = USB Connectors [package=usb-a-pcb]
  CAMERA1 = TTL Serial JPEG Camera
  DC_Mot_Enc2 = DC Motor with two-phase hall-encoder [part_number=VT-E-G25A-06-177E]
  DC_Mot_Enc3 = DC Motor with two-phase hall-encoder [part_number=VT-E-G25A-06-177E]
  M1 = DC Motor
  VALVE1 = Plastic Solenoid Valve

nets:
  N1: Part1.D21/SCL, DC_Mot_Enc2.pin3
  N2: Part1.D20/SDA, DC_Mot_Enc2.pin4
  N3: Part1.D19/RX1, DC_Mot_Enc1.pin3
  N4: Part1.D18/TX1, DC_Mot_Enc1.pin4
  GND: Part1.GND, S1.GND, S2.GND, BATT1.negative, U1.GND, U1.K1-In, DC_Mot_Enc1.pin2, DC_Mot_Enc2.pin2, DC_Mot_Enc3.pin2
  5V: Part1.5V, S1.5V, S2.5V, U1.VCC, DC_Mot_Enc1.pin1, DC_Mot_Enc2.pin1, DC_Mot_Enc3.pin1
  N5: Part1.D2_PWM, DC_Mot_Enc3.pin3
  N6: Part1.D3_PWM, DC_Mot_Enc3.pin4
  N7: Part1.D4_PWM, S2.ENA
  N8: Part1.D5_PWM, S2.ENB
  N9: Part1.D6_PWM, S1.ENA
  N10: Part1.D7_PWM, S1.ENB
  N11: Part1.D22, S2.IN1
  N12: Part1.D23, S2.IN2
  N13: Part1.D24, S2.IN3
  N14: Part1.D25, S2.IN4
  N15: Part1.D26, S1.IN1
  N16: Part1.D27, S1.IN2
  N17: Part1.D28, S1.IN3
  N18: Part1.D29, S1.IN4
  N19: Part1.D32, U1.IN1
  N20: Part1.D33, U1.IN2
  12V: S1.12V, S2.12V, BATT1.positive
  N21: S1.M1-01, DC_Mot_Enc1.pin6
  N22: S1.M1-02, DC_Mot_Enc1.pin5
  N23: S1.M2-01, M1.pin_2
  N24: S1.M2-02, M1.pin_1
  N25: S1.ENB-5V, U1.K2-In
  N26: S2.M1-01, DC_Mot_Enc3.pin6
  N27: S2.M1-02, DC_Mot_Enc3.pin5
  N28: S2.M2-01, DC_Mot_Enc2.pin5
  N29: S2.M2-02, DC_Mot_Enc2.pin6
  N30: U1.K1-Off, U1.K2-On, VALVE1.no_name_yet#2
  N31: U1.K1-On, U1.K2-Off, VALVE1.no_name_yet#1
  N32: X1.D-, CAMERA1.TX
  N33: X2.D+, X3.GND

notes:
  camera module
  motor colour code here:
  red: Vcc
  black: Gnd
  yellow: EncA
  green: EncB
  blue: motor +
  grey: motor -
  For the actual colour code check out motor datasheet
  Vaccum pump
  x-dir motor
  y-dir motor
  z-dir motor
  Solenoid Valve

custom parts:
  H-Bridge with L298N: h-bridge
  LiPoly Battery (1300mAh): Lithium Ion Polymer Battery (1300mAh)
  2-Channel 5v Relay Shield: 2 Channel 5v Relay Shield w. 2x SPD-06VDC-SD-C
  TTL Serial JPEG Camera: TTL Serial JPEG Camera with NTSC Out
